# Fritzing sketch Schematic (saved by Fritzing 0.9.3b)
breadboards: 1

parts:
  Part3 = Arduino Nano (Rev3.0)
  U2 = Voltage Regulator - 5V [package="TO220 [THT]"]
  VCC4 = Battery block 9V
  L293D2 = L293D [package=THT]
  DC_Motor3 = DC Motor
  DC_Motor4 = DC Motor
  VCC5 = Battery block 9V
  Part4 = SRF05 Ultrasonic Rangefinder
  Part5 = MAG3110

nets:
  GND: Part3.GND, U2.GND, VCC4.-, L293D2.0V, VCC5.-, Part4.GND, Part5.GND
  N1: Part3.D2, Part4.Echo
  N2: Part3.D3, Part4.Trig
  N3: Part3.D5, L293D2.Enable_1
  N4: Part3.D6, L293D2.In_1
  N5: Part3.D8, L293D2.In_2
  N6: Part3.D9, L293D2.Enable_2
  N7: Part3.D10, L293D2.In_3
  N8: Part3.D11/MOSI, L293D2.In_4
  VIN: Part3.VIN, U2.output_voltage, Part5.VCC
  5V: Part3.5V, L293D2.+Vmotor, Part4.VCC
  N9: Part3.A5, Part5.SCL
  N10: Part3.A4, Part5.SDA
  N11: U2.input_voltage, VCC4.+
  N12: L293D2.Out_1_(_Controlled_by_Enable_1_), DC_Motor3.pin_1
  N13: L293D2.Out_2_(_Controlled_by_Enable_1_), DC_Motor3.pin_2
  N14: L293D2.Out_3_(_Controlled_by_Enable_2_), DC_Motor4.pin_1
  N15: L293D2.Out_4_(_Controlled_by_Enable_2_), DC_Motor4.pin_2
  N16: L293D2.+V, VCC5.+

custom parts:
  MAG3110: Description: Freescale’s MAG3110 is a small, low-power, digital 3-axis magnetometer. The device can be used in conjunction with a 3-axis accelerometer to produce orientation independent accurate compass heading information. It features a standard I2C serial interface output and smart embedded functions. It’s also a tiny QFN package which isn’t very easy to play with so here is our easy to use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
