# Fritzing sketch boat (saved by Fritzing 0.9.3b)
breadboards: 1

parts:
  HC-SR04_Sensor_1 = HC-SR04 Ultrasonic Distance Sensor
  U1 = MAG3110 [package=dfn-10]  # not connected
  U2 = L298_BRIDGE_DRIVER [package=powerso20]  # not connected
  Nano1 = Arduino Nano v2.3
  VCC1 = Battery  # not connected
  R1 = Resistor [tolerance=±5% resistance=220 package="0805 [SMD]"]
  R2 = Resistor [tolerance=±5% resistance=220 package="0805 [SMD]"]

nets:
  VCC: HC-SR04_Sensor_1.VCC, Nano1.VIN
  N1: HC-SR04_Sensor_1.TRIG, Nano1.D3, R1.Pin_0
  N2: HC-SR04_Sensor_1.ECHO, Nano1.D2, R2.Pin_0
  GND: HC-SR04_Sensor_1.GND, Nano1.GND, R1.Pin_1, R2.Pin_1
